// Logisim project bbjj_cpu.circ as structural Verilog: 1 circuit, main circuit main
module main (
);

  wire button_1_out, CLOCK_out, comparator_1_eq, comparator_2_lt, not_1_out, or_1_out, or_2_out, or_3_out,
       or_4_out, or_5_out, PHASE1_out, PHASE2_out, PHASE3_out, ProgramPathSelector_q, register_6_q,
       shift_register_1_out, shift_register_1_q0, shift_register_1_q2, shift_register_1_q3;
  wire [0:0] multiplexer_3_out;
  wire [3:0] ram_1_data;
  wire [7:0] multiplexer_1_out, multiplexer_2_out, register_1_q, register_2_q, register_3_q, register_4_q,
       register_5_q;
  wire [31:0] rom_1_data;

  Register #(.width(1), .trigger("high")) ProgramPathSelector (
    .D(multiplexer_3_out[0]), .en(comparator_1_eq), .Q(ProgramPathSelector_q), .clk(or_4_out));  // open: clr
  Multiplexer #(.width(8), .enable("false")) multiplexer_1 (
    .in0(register_2_q), .in1(register_3_q), .out(multiplexer_1_out), .sel(ProgramPathSelector_q));
  Button button_1 (.out(button_1_out));
  Shift_Register #(.length(4)) shift_register_1 (
    .in(shift_register_1_out), .clk(CLOCK_out), .out(shift_register_1_out), .load(button_1_out), .d0(1'b0),
    .q0(shift_register_1_q0), .d1(1'b0), .d2(1'b0), .q2(shift_register_1_q2), .d3(1'b1),
    .q3(shift_register_1_q3));  // open: shift, clr, q1
  Clock CLOCK (.out(CLOCK_out));
  Button PHASE1 (.out(PHASE1_out));
  Register register_1 (.D(multiplexer_1_out), .Q(register_1_q), .clk(or_1_out));  // open: en, clr
  or or_1 (or_1_out, or_3_out, or_2_out);
  or or_2 (or_2_out, shift_register_1_q0, PHASE1_out);
  Button PHASE3 (.out(PHASE3_out));
  or or_3 (or_3_out, PHASE3_out, shift_register_1_q3);
  ROM #(.dataWidth(32)) rom_1 (.addr(register_1_q), .data(rom_1_data));  // open: sel
  Register register_2 (.D(rom_1_data[23:16]), .Q(register_2_q), .clk(or_2_out));  // open: en, clr
  Register register_3 (.D(rom_1_data[31:24]), .Q(register_3_q), .clk(or_2_out));  // open: en, clr
  Register register_4 (.D(rom_1_data[7:0]), .Q(register_4_q), .clk(or_2_out));  // open: en, clr
  Register register_5 (.D(rom_1_data[15:8]), .Q(register_5_q), .clk(or_2_out));  // open: en, clr
  Multiplexer #(.width(8), .enable("false")) multiplexer_2 (
    .in0(register_4_q), .in1(register_5_q), .out(multiplexer_2_out), .sel(not_1_out));
  not not_1 (not_1_out, or_2_out);
  Button PHASE2 (.out(PHASE2_out));
  Comparator #(.mode("unsigned")) comparator_1 (.a(8'h2), .b(register_5_q), .eq(comparator_1_eq));  // open: gt, lt
  or or_4 (or_4_out, shift_register_1_q2, PHASE2_out);
  RAM #(.dataWidth(4), .bus("separate")) ram_1 (
    .addr(multiplexer_2_out), .din({3'b000, multiplexer_3_out[0]}),
    .data({{3{ram_1_data[3]}}, ram_1_data[0]}), .str(or_4_out), .clk(or_4_out), .ld(or_2_out));  // open: sel, clr
  or or_5 (or_5_out, or_4_out, or_2_out);
  Comparator #(.mode("unsigned")) comparator_2 (.a(register_4_q), .b(8'h2), .lt(comparator_2_lt));  // open: gt, eq
  Register #(.width(1), .trigger("high")) register_6 (
    .D(ram_1_data[0]), .Q(register_6_q), .clk(or_5_out));  // open: en, clr
  Multiplexer #(.enable("false")) multiplexer_3 (
    .in0(register_6_q), .in1(register_4_q[0]), .out(multiplexer_3_out[0]), .sel(comparator_2_lt));
  // also tied to GND on the sheet: ram_1_data[3]

  // Notes on the sheet:
  //   SELECT IP
  //   INSTRUCTION POINTER (IP)
  //   ROM (PROGRAM)
  //   contents of rom_1 (hex, n*v repeats v):
  //   1000201 1000200
  //   COPY_TO
  //   COPY_FROM
  //   IP_CASE_0
  //   IP_CASE_1
  //   RAM (DATA)
endmodule
